// Digital circuit Add_8bits.dig as structural Verilog
module Add_8bits (
  input  [7:0] A,
  input  [7:0] B,
  output C0,
  output [7:0] S
);

  wire full_add_1_co, full_add_2_co, full_add_3_co, full_add_4_co, full_add_5_co, full_add_6_co,
       full_add_7_co;

  Full_add full_add_1 (.A(A[0]), .B(B[0]), .Ci(1'b0), .S(S[0]), .Co(full_add_1_co));
  Full_add full_add_2 (.A(A[1]), .B(B[1]), .Ci(full_add_1_co), .S(S[1]), .Co(full_add_2_co));
  Full_add full_add_3 (.A(A[2]), .B(B[2]), .Ci(full_add_2_co), .S(S[2]), .Co(full_add_3_co));
  Full_add full_add_4 (.A(A[3]), .B(B[3]), .Ci(full_add_3_co), .S(S[3]), .Co(full_add_4_co));
  Full_add full_add_5 (.A(A[4]), .B(B[4]), .Ci(full_add_4_co), .S(S[4]), .Co(full_add_5_co));
  Full_add full_add_6 (.A(A[5]), .B(B[5]), .Ci(full_add_5_co), .S(S[5]), .Co(full_add_6_co));
  Full_add full_add_7 (.A(A[6]), .B(B[6]), .Ci(full_add_6_co), .S(S[6]), .Co(full_add_7_co));
  Full_add full_add_8 (.A(A[7]), .B(B[7]), .Ci(full_add_7_co), .S(S[7]), .Co(C0));

  // Other names for the same wires on the sheet: A1 = A[0]; A2 = A[1]; A3 = A[2]; A4 = A[3]; A5 = A[4]; A6 = A[5];
  //   A7 = A[6]; A8 = A[7]; B1 = B[0]; B2 = B[1]; B3 = B[2]; B4 = B[3]; B5 = B[4]; B6 = B[5]; B7 = B[6]; B8 = B[7]
endmodule
