// Digital circuit ALU.dig as structural Verilog
module ALU (
  input  [7:0] A,
  input  [7:0] B,
  input  [1:0] Sel,
  output [7:0] Out,
  output [7:0] R,
  output plus
);

  wire m01;
  wire [7:0] m0, m1, m02, m2, m3;

  Subtract_negative subtract_negative_1 (.A(A), .B(B), .Subtract(m0), .Signal(m01));
  Add_8bits add_8bits_1 (.A(A), .B(B), .S(m1));  // open: C0
  Divider_8bits divider_8bits_1 (.D(A), .d_2(B), .q(m2), .r(m02));
  Times_8bits times_8bits_1 (.A(A[3:0]), .B(B[3:0]), .Times(m3));
  Multiplexer #(.Selector_Bits(2)) multiplexer_1 (
    .sel(Sel), .in_0(m01), .in_1(1'b0), .in_2(1'b0), .in_3(1'b0), .out(plus));
  Multiplexer #(.Selector_Bits(2), .Bits(8)) multiplexer_2 (
    .sel(Sel), .in_0({8{1'b0}}), .in_1({8{1'b0}}), .in_2(m02), .in_3({8{1'b0}}), .out(R));
  Multiplexer #(.Selector_Bits(2), .Bits(8)) multiplexer_3 (
    .sel(Sel), .in_0(m0), .in_1(m1), .in_2(m2), .in_3(m3), .out(Out));

  // Other names for the same wires on the sheet: AT[3:0] = A[3:0]; BT[3:0] = B[3:0]; S[1:0] = Sel
endmodule
