// Digital circuit CC.dig as structural Verilog
module CC (
  input  [7:0] I,
  input  [3:0] Rn,
  output Nlo,
  output Nlb,
  output Eu,
  output Su1,
  output Su0,
  output NLa,
  output Ncl,
  output NLi,
  output NCE,
  output NLm,
  output Ep,
  output Cp
);

  wire [11:0] Instructions_d;

  ROM #(.AddrBits(8), .Bits(12)) Instructions (.A(I), .sel(1'b1), .D(Instructions_d));
  assign {Cp, Ep, NLm, NCE, NLi, Ncl, NLa, Su0, Su1, Eu, Nlb, Nlo} = Rn[3] ? Instructions_d : 12'bz;  // Driver driver_1
  assign {Cp, Ep, NLm, NCE, NLi, Ncl, NLa, Su0, Su1, Eu, Nlb, Nlo} = Rn[2] ? 12'h263 : 12'bz;  // Driver driver_2
  assign {Cp, Ep, NLm, NCE, NLi, Ncl, NLa, Su0, Su1, Eu, Nlb, Nlo} = Rn[1] ? 12'hbe3 : 12'bz;  // Driver driver_3
  assign {Cp, Ep, NLm, NCE, NLi, Ncl, NLa, Su0, Su1, Eu, Nlb, Nlo} = Rn[0] ? 12'h5e3 : 12'bz;  // Driver driver_4

  // Notes on the sheet:
  //   contents of Instructions (hex, n*v repeats v):
  //   5e3,2e1,5e3,2c3,3e6,3a3
endmodule
