// Digital circuit CPU.dig as structural Verilog
module CPU (
  input  clk,
  input  clk_2
);

  wire Cp, Ep, Eu, Execute, Fetch, NCe, Ncl, Nla, Nlb, NLi, NLm, Nlo, not_1_out, not_2_out, or_1_out,
       plus____out, Su_0, Su_1;
  wire [1:0] full_rc_1_q;
  wire [3:0] Din_0, Din_1, R_out1, R_out2;
  wire [7:0] A_A, A_B, alu_1_out, B_in, IR, IR_q, MAR_q, Out, PC_out;

  // Probe on B_in
  Register #(.Bits(8)) MAR (.D(B_in), .C(NLm), .en(1'b1), .Q(MAR_q));
  Full_RC full_rc_1 (.Clk(clk), .Q({Execute, Fetch, full_rc_1_q}));
  not not_1 (not_1_out, NCe);
  // Probe on MAR_q
  ROM #(.AddrBits(8), .Bits(8)) rom_1 (.A(MAR_q), .sel(not_1_out), .D(Out));
  // Probe on {Execute, Fetch, full_rc_1_q}
  // Probe on IR
  CC cc_1 (
    .I(IR), .Rn({Execute, Fetch, full_rc_1_q}), .Nlo(Nlo), .Nlb(Nlb), .Eu(Eu), .Su1(Su_1), .Su0(Su_0),
    .NLa(Nla), .Ncl(Ncl), .NLi(NLi), .NCE(NCe), .NLm(NLm), .Ep(Ep), .Cp(Cp));
  not not_2 (not_2_out, Ncl);
  or or_1 (or_1_out, Ep, Eu, ~NCe);  // Or
  Register #(.Bits(8)) u_IR (.D(B_in), .C(clk_2), .en(~NLi), .Q(IR_q));
  Counter #(.Bits(8)) PC (.en(1'b1), .C(Cp), .clr(not_2_out), .out(PC_out));  // open: ovf
  // Probe on Out
  Register #(.Bits(8)) Bus_w (.D(Out), .C(clk_2), .en(or_1_out), .Q(B_in));
  // Probe on PC_out
  assign Out = Ep ? PC_out : 8'bz;  // Driver driver_1
  // Probe on B_in
  // Probe on IR
  assign IR = Execute ? IR_q : 8'bz;  // Driver driver_2
  // Probe on Out
  // Probe on A_A
  Register #(.Bits(8)) AC (.D(B_in), .C(clk_2), .en(~Nla), .Q(A_A));
  // Probe on A_B
  ALU alu_1 (.A(A_A), .B(A_B), .Sel({Su_1, Su_0}), .Out(alu_1_out), .R({R_out2, R_out1}), .plus(plus____out));
  // Probe on B_in
  Register #(.Bits(8)) B (.D(B_in), .C(clk_2), .en(~Nlb), .Q(A_B));
  // Probe on B_in
  Register #(.Bits(8)) u_Out (.D(B_in), .C(clk_2), .en(~Nlo), .Q({Din_1, Din_0}));
  // Probe on A_A
  assign Out = Eu ? alu_1_out : 8'bz;  // Driver driver_3
  // Probe on A_B
  // Probe on Out
  LED led_1 (.in(plus____out));
  Seven_Seg_Hex seven_seg_hex_1 (.d(Din_1), .dp(1'b0));
  Seven_Seg_Hex seven_seg_hex_2 (.d(R_out2), .dp(1'b0));
  Seven_Seg_Hex seven_seg_hex_3 (.d(Din_0), .dp(1'b0));
  Seven_Seg_Hex seven_seg_hex_4 (.d(R_out1), .dp(1'b0));

  // Other names for the same wires on the sheet: Clk_t = clk_2; RC = clk

  // Notes on the sheet:
  //   clk_2: Hz: 5
  //   contents of rom_1 (hex, n*v repeats v):
  //   0,1,2,3,4,5,123*0,1,2,3,4,5
endmodule
