// Digital circuit Divider_8bits.dig as structural Verilog
module Divider_8bits (
  input  [7:0] D,
  input  [7:0] d_2,
  output [7:0] q,
  output [7:0] r
);

  wire nq0, nq1, nq2, nq3, nq4, nq5, nq6, nq7;
  wire [7:0] multiplexer_1_out, multiplexer_2_out, multiplexer_3_out, multiplexer_4_out, multiplexer_5_out,
       multiplexer_6_out, multiplexer_7_out, op0, op1, op2, op3, op4, op5, op6, op7, s0, s1, s2, s3, s4, s5,
       s6, s7;

  assign q = ~{nq7, nq6, nq5, nq4, nq3, nq2, nq1, nq0};  // Not not_1, 8 bits wide
  shift_left shift_left_1 (.A({8{1'b0}}), .Shift(D[7]), .gt__gt_A(op7));
  Multiplexer #(.Bits(8)) multiplexer_1 (.sel(nq7), .in_0(s7), .in_1(op7), .out(multiplexer_1_out));
  Multiplexer #(.Bits(8)) multiplexer_2 (.sel(nq6), .in_0(s6), .in_1(op6), .out(multiplexer_2_out));
  Multiplexer #(.Bits(8)) multiplexer_3 (.sel(nq5), .in_0(s5), .in_1(op5), .out(multiplexer_3_out));
  Multiplexer #(.Bits(8)) multiplexer_4 (.sel(nq4), .in_0(s4), .in_1(op4), .out(multiplexer_4_out));
  Multiplexer #(.Bits(8)) multiplexer_5 (.sel(nq3), .in_0(s3), .in_1(op3), .out(multiplexer_5_out));
  Multiplexer #(.Bits(8)) multiplexer_6 (.sel(nq2), .in_0(s2), .in_1(op2), .out(multiplexer_6_out));
  Multiplexer #(.Bits(8)) multiplexer_7 (.sel(nq1), .in_0(s1), .in_1(op1), .out(multiplexer_7_out));
  shift_left shift_left_2 (.A(multiplexer_1_out), .Shift(D[6]), .gt__gt_A(op6));
  shift_left shift_left_3 (.A(multiplexer_2_out), .Shift(D[5]), .gt__gt_A(op5));
  shift_left shift_left_4 (.A(multiplexer_3_out), .Shift(D[4]), .gt__gt_A(op4));
  shift_left shift_left_5 (.A(multiplexer_4_out), .Shift(D[3]), .gt__gt_A(op3));
  shift_left shift_left_6 (.A(multiplexer_5_out), .Shift(D[2]), .gt__gt_A(op2));
  shift_left shift_left_7 (.A(multiplexer_6_out), .Shift(D[1]), .gt__gt_A(op1));
  shift_left shift_left_8 (.A(multiplexer_7_out), .Shift(D[0]), .gt__gt_A(op0));
  Multiplexer #(.Bits(8)) multiplexer_8 (.sel(nq0), .in_0(s0), .in_1(op0), .out(r));
  Sub #(.Bits(8)) sub_1 (.a(op7), .b(d_2), .c_i(1'b0), .s(s7), .c_o(nq7));
  Sub #(.Bits(8)) sub_2 (.a(op6), .b(d_2), .c_i(1'b0), .s(s6), .c_o(nq6));
  Sub #(.Bits(8)) sub_3 (.a(op5), .b(d_2), .c_i(1'b0), .s(s5), .c_o(nq5));
  Sub #(.Bits(8)) sub_4 (.a(op4), .b(d_2), .c_i(1'b0), .s(s4), .c_o(nq4));
  Sub #(.Bits(8)) sub_5 (.a(op3), .b(d_2), .c_i(1'b0), .s(s3), .c_o(nq3));
  Sub #(.Bits(8)) sub_6 (.a(op2), .b(d_2), .c_i(1'b0), .s(s2), .c_o(nq2));
  Sub #(.Bits(8)) sub_7 (.a(op1), .b(d_2), .c_i(1'b0), .s(s1), .c_o(nq1));
  Sub #(.Bits(8)) sub_8 (.a(op0), .b(d_2), .c_i(1'b0), .s(s0), .c_o(nq0));

  // Other names for the same wires on the sheet: d_t[7:0] = d_2
endmodule
