// Digital circuit Full_RC.dig as structural Verilog
module Full_RC (
  input  Clk,
  output [3:0] Q
);

  wire and_1_out;
  wire [1:0] counter_1_out;

  Counter #(.Bits(2)) counter_1 (.en(1'b1), .C(Clk), .clr(1'b0), .out(counter_1_out));  // open: ovf
  and and_1 (and_1_out, ~counter_1_out[0], ~counter_1_out[1]);  // And
  Ring_counter ring_counter_1 (.Clk(Clk), .D(and_1_out), .Q(Q));
endmodule
