// Digital circuit Pc.dig as structural Verilog
module Pc (
  input  Clr,
  input  Cp,
  input  Ep,
  output [7:0] Out
);

  wire multiplexer_2_out;
  wire [7:0] add_8bits_1_s, multiplexer_1_out, register_1_q, subtract_negative_1_subtract;

  Add_8bits add_8bits_1 (.A(register_1_q), .B(8'h1), .S(add_8bits_1_s));  // open: C0
  Subtract_negative subtract_negative_1 (
    .A(add_8bits_1_s), .B(add_8bits_1_s), .Subtract(subtract_negative_1_subtract));  // open: Signal
  Multiplexer #(.Bits(8)) multiplexer_1 (
    .sel(Clr), .in_0(add_8bits_1_s), .in_1(subtract_negative_1_subtract), .out(multiplexer_1_out));
  Multiplexer multiplexer_2 (.sel(Clr), .in_0(Cp), .in_1(Clr), .out(multiplexer_2_out));
  Register #(.Bits(8)) register_1 (.D(multiplexer_1_out), .C(multiplexer_2_out), .en(1'b1), .Q(register_1_q));
  assign Out = Ep ? register_1_q : 8'bz;  // Driver driver_1
endmodule
