// Digital circuit Subtract_8bits.dig as structural Verilog
module Subtract_8bits (
  input  [7:0] B,
  input  [7:0] A,
  output [7:0] Subtract,
  output C0
);

  wire [7:0] add_8bits_1_s, not_1_out;

  assign not_1_out = ~B;  // Not not_1, 8 bits wide
  Add_8bits add_8bits_1 (.A(not_1_out), .B(8'h1), .S(add_8bits_1_s));  // open: C0
  Add_8bits add_8bits_2 (.A(A), .B(add_8bits_1_s), .C0(C0), .S(Subtract));
endmodule
