// Digital circuit Subtract_negative.dig as structural Verilog
module Subtract_negative (
  input  [7:0] A,
  input  [7:0] B,
  output [7:0] Subtract,
  output Signal
);

  wire [6:0] subtract_8bits_1_subtract;
  wire [7:0] add_8bits_1_s, not_1_out;

  Subtract_8bits subtract_8bits_1 (.B(A), .A(B), .Subtract({Signal, subtract_8bits_1_subtract}));  // open: C0
  assign not_1_out = ~{Signal, subtract_8bits_1_subtract};  // Not not_1, 8 bits wide
  Add_8bits add_8bits_1 (.A(not_1_out), .B(8'h1), .S(add_8bits_1_s));  // open: C0
  assign Subtract = Signal ? add_8bits_1_s : 8'bz;  // Driver driver_1
  assign Subtract = ~Signal ? {Signal, subtract_8bits_1_subtract} : 8'bz;  // DriverInvSel driverinvsel_1
endmodule
