// Digital circuit Ring_counter.dig as structural Verilog
module Ring_counter (
  input  Clk,
  input  D,
  output [3:0] Q
);

  D_FF d_ff_1 (.D(D), .C(Clk), .Q(Q[0]));  // open: nQ
  D_FF d_ff_2 (.D(Q[0]), .C(Clk), .Q(Q[1]));  // open: nQ
  D_FF d_ff_3 (.D(Q[1]), .C(Clk), .Q(Q[2]));  // open: nQ
  D_FF d_ff_4 (.D(Q[2]), .C(Clk), .Q(Q[3]));  // open: nQ
endmodule
